# Fritzing sketch ROV (saved by Fritzing 0.9.3b)
breadboards: 1
perfboards: 1

parts:
  Part1 = Arduino Mega 2560 (Rev3)
  Camera_Tilt = Basic Servo
  Camera_Pan = Basic Servo

nets:
  GND: Part1.GND, Camera_Tilt.gnd, Camera_Pan.gnd
  VCC: Part1.5V, Camera_Tilt.vcc, Camera_Pan.vcc
