# Fritzing sketch diodeboard_01 (saved by Fritzing 0.9.3b)
circuit board: 9.05cm x 7cm
breadboards: 2

parts:
  J1 = Camdenboss CTB0158-4 [part_number=CTB0158-4 package=THT]
  J2 = Camdenboss CTB0158-6 [part_number=CTB0158-6 package=THT]
  D26 = Rectifier Diode [part_number=1N4001 package="300 mil [THT]"]
  D27 = Rectifier Diode [part_number=1N4001 package="300 mil [THT]"]
  D28 = Rectifier Diode [part_number=1N4001 package="300 mil [THT]"]
  D29 = Rectifier Diode [part_number=1N4001 package="300 mil [THT]"]
  D30 = Rectifier Diode [part_number=1N4001 package="300 mil [THT]"]
  D31 = Rectifier Diode [part_number=1N4001 package="300 mil [THT]"]
  D32 = Rectifier Diode [part_number=1N4001 package="300 mil [THT]"]
  D33 = Rectifier Diode [part_number=1N4001 package="300 mil [THT]"]
  D34 = Rectifier Diode [part_number=1N4001 package="300 mil [THT]"]
  D35 = Rectifier Diode [part_number=1N4001 package="300 mil [THT]"]
  D36 = Rectifier Diode [part_number=1N4001 package="300 mil [THT]"]
  D37 = Rectifier Diode [part_number=1N4001 package="300 mil [THT]"]

nets:
  N1: J1.pin1, D26.anode, D27.anode, D28.anode
  N2: J1.pin2, D29.anode, D30.anode, D31.anode
  N3: J1.pin3, D32.anode, D33.anode, D34.anode
  N4: J1.pin4, D35.anode, D36.anode, D37.anode
  N5: J2.pin1, D27.cathode, D37.cathode
  N6: J2.pin2, D30.cathode, D32.cathode
  N7: J2.pin3, D31.cathode, D36.cathode
  N8: J2.pin4, D26.cathode, D33.cathode
  N9: J2.pin5, D28.cathode, D29.cathode
  N10: J2.pin6, D34.cathode, D35.cathode

notes:
  Randy Hawkins
  v1.0  Dec. 2016
  Mapping Diode Board
  Joystick-To-Motor
  InDeep
  Rotate Right
  Forward
  4
  3
  2
  1
  1 = Front Left
  2 = Front Right
  3 = Back Left
  4 = Back Right
  Backward
  Left
  Rotate Left
  Right
